# Fritzing sketch Chapter1 (saved by Fritzing 0.9.2b)
breadboards: 1

parts:
  Part1 = Arduino Uno (Rev3)
  R5 = Resistor [tolerance=±5% resistance=220 package=THT]
  LED6 = LED - 5mm [color="Red (633nm)" package="5 mm [THT]"]
  J1 = Piezo Speaker
  U2 = POT [package=pot_mammoth]

nets:
  N1: Part1.A0, U2.A
  N2: Part1.D8, J1.pin2
  N3: Part1.D2, LED6.anode
  N4: Part1.5V, U2.E
  N5: Part1.GND, R5.Pin_1, J1.pin1, U2.S
  N6: R5.Pin_0, LED6.cathode
