# Fritzing sketch Chapter2 (saved by Fritzing 0.9.2b)
breadboards: 1

parts:
  Part1 = Arduino Uno (Rev3)
  Part2 = Arduino Cap Sense Shield
  LCD1 = LCD screen

nets:
  N1: Part1.D8, LCD1.DB7
  N2: Part1.D2, Part2.q5
  N3: Part1.D3_PWM, LCD1.RS
  N4: Part1.D4, LCD1.E
  N5: Part1.D5_PWM, LCD1.DB4
  N6: Part1.D6_PWM, LCD1.DB5
  N7: Part1.D7, LCD1.DB6
  5V: Part1.5V, Part2.q4, LCD1.VDD
  GND: Part1.GND, LCD1.VSS, LCD1.V0, LCD1.R/W

custom parts:
  Arduino Cap Sense Shield: Description: The MPR121 IC is a great way to build simple capacitive touch interfaces, and now it's even easier to incorporate into your Arduino projects with the touch shield. The touch shield has 9 capacitive touch pads, with headers for the remaining 3 electrode connections. With this shield you can have a total of 12 touch sensitive buttons. An on-board logic level converter allows it to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
