# Fritzing sketch Chapter3 (saved by Fritzing 0.9.2b)
breadboards: 1

parts:
  Part1 = Arduino Uno (Rev3)
  J1 = Piezo Speaker
  R1 = Resistor [tolerance=±5% resistance=220 package=THT]
  LED2 = LED - 5mm [color="Red (633nm)" package="5 mm [THT]"]
  R2 = Resistor [tolerance=±5% resistance=220 package=THT]
  Part2 = Arduino Cap Sense Shield
  LED1 = smd LED [color="Green (555nm)" package="0805 [SMD]"]  # not connected
  Part3 = SRF05 Ultrasonic Rangefinder

nets:
  N1: Part1.D8, J1.pin2
  N2: Part1.D9_PWM, Part3.Trig
  N3: Part1.D10_PWM/SS, Part3.Echo
  GND: Part1.GND, J1.pin1, R1.Pin_0, R2.Pin_0, Part3.GND
  N4: Part1.D3_PWM, Part2.q5
  5V: Part1.5V, Part2.q4, Part3.VCC
  N5: LED2.cathode, R2.Pin_1

custom parts:
  Arduino Cap Sense Shield: Description: The MPR121 IC is a great way to build simple capacitive touch interfaces, and now it's even easier to incorporate into your Arduino projects with the touch shield. The touch shield has 9 capacitive touch pads, with headers for the remaining 3 electrode connections. With this shield you can have a total of 12 touch sensitive buttons. An on-board logic level converter allows it to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
