# Fritzing sketch Chapter5 (saved by Fritzing 0.9.2b)
breadboards: 1

parts:
  Part1 = Arduino Uno (Rev3)
  U1 = POT [package=pot_mammoth]  # not connected
  U2 = ESP8266 WiFi Module [part_number=ESP8266]

nets:
  N1: Part1.D8, U2.CH_PD
  N2: Part1.D9_PWM, U2.TXD
  N3: Part1.3V3, U2.RST
  5V: Part1.5V, U2.VCC

custom parts:
  ESP8266 WiFi Module: Generic WiFi Module based on the ESP8266 with onboard PCB antenna and UART communications
